// Logisim project EMDS.circ as structural Verilog: 6 circuits, main circuit main
module main (
);

  wire _0_2_out, _0_out, _1_2_out, _1_out, and_1_out, and_2_out, clock_1_out, clock_2_out, keyboard_1_avail,
       keyboard_2_avail, messenger_1_display_clock, messenger_1_incoming_monitor_clock,
       messenger_1_outgoing_message, messenger_1_output_command, messenger_2_display_clock,
       messenger_2_incoming_monitor_clock, messenger_2_outgoing_message, messenger_2_output_command,
       password_checker_1_verified_output, password_checker_2_verified_output, X_2_out, X_out;
  wire [6:0] keyboard_1_data, keyboard_2_data, messenger_1_encrypted_text, messenger_1_incoming_monitor,
       messenger_1_outgoing_monitor, messenger_2_encrypted_text, messenger_2_incoming_monitor,
       messenger_2_outgoing_monitor;

  Clock clock_1 (.out(clock_1_out));
  and and_1 (and_1_out, clock_1_out, password_checker_1_verified_output);
  TTY tty_1 (.data(messenger_1_incoming_monitor), .clk(messenger_1_incoming_monitor_clock));  // open: we, clr
  TTY tty_2 (.data(messenger_1_encrypted_text), .clk(and_1_out));  // open: we, clr
  Password_Checker password_checker_1 (
    .Switch_Off(X_out), .Clock(clock_1_out), ._0_Button(_0_out), ._1_Button(_1_out),
    .Verified_Output(password_checker_1_verified_output));
  Button _0 (.out(_0_out));
  Button X (.out(X_out));
  Button _1 (.out(_1_out));
  // Probe on 7'b1000011
  LED led_1 (.in(password_checker_1_verified_output));
  TTY tty_3 (.data(messenger_1_outgoing_monitor), .clk(messenger_1_display_clock));  // open: we, clr
  Keyboard keyboard_1 (
    .clk(messenger_1_display_clock), .avail(keyboard_1_avail), .data(keyboard_1_data));  // open: re, clr
  Messenger messenger_1 (
    .Clock(and_1_out), .Key(7'b1000011), .Enable(1'b1), .Outgoing_message(messenger_1_outgoing_message),
    .Output_command(messenger_1_output_command), .Output_Clock(messenger_2_output_command),
    .Incoming_Message(messenger_2_outgoing_message),
    .Incoming_Monitor_Clock(messenger_1_incoming_monitor_clock),
    .Incoming_Monitor(messenger_1_incoming_monitor), .Display_CLock(messenger_1_display_clock),
    .Keyboard_IA(keyboard_1_avail), .Keyboard_Input(keyboard_1_data),
    .Outgoing_Monitor(messenger_1_outgoing_monitor), .Encrypted_Text(messenger_1_encrypted_text));
  Clock clock_2 (.out(clock_2_out));
  and and_2 (and_2_out, clock_2_out, password_checker_2_verified_output);
  TTY tty_4 (.data(messenger_2_incoming_monitor), .clk(messenger_2_incoming_monitor_clock));  // open: we, clr
  Button X_2 (.out(X_2_out));
  Password_Checker password_checker_2 (
    .Switch_Off(X_2_out), .Clock(clock_2_out), ._0_Button(_0_2_out), ._1_Button(_1_2_out),
    .Verified_Output(password_checker_2_verified_output));
  Button _1_2 (.out(_1_2_out));
  Button _0_2 (.out(_0_2_out));
  // Probe on 7'b1000011
  LED led_2 (.in(password_checker_2_verified_output));
  TTY tty_5 (.data(messenger_2_outgoing_monitor), .clk(messenger_2_display_clock));  // open: we, clr
  TTY tty_6 (.data(messenger_2_encrypted_text), .clk(and_2_out));  // open: we, clr
  Keyboard keyboard_2 (
    .clk(messenger_2_display_clock), .avail(keyboard_2_avail), .data(keyboard_2_data));  // open: re, clr
  Messenger messenger_2 (
    .Clock(and_2_out), .Key(7'b1000011), .Enable(1'b1), .Outgoing_message(messenger_2_outgoing_message),
    .Output_command(messenger_2_output_command), .Output_Clock(messenger_1_output_command),
    .Incoming_Message(messenger_1_outgoing_message),
    .Incoming_Monitor_Clock(messenger_2_incoming_monitor_clock),
    .Incoming_Monitor(messenger_2_incoming_monitor), .Display_CLock(messenger_2_display_clock),
    .Keyboard_IA(keyboard_2_avail), .Keyboard_Input(keyboard_2_data),
    .Outgoing_Monitor(messenger_2_outgoing_monitor), .Encrypted_Text(messenger_2_encrypted_text));

  // Notes on the sheet:
  //   ENCRYPTED MESSAGE OF B
  //   INCOMING TEXT
  //   Enter Password
  //   Password Correct Checker Light
  //   OUTGOING TEXT
  //   INCOMING TEXT
  //   Enter Password
  //   Password Correct Checker Light
  //   ENCRYPTED MESSAGE OF A
  //   OUTGOING TEXT
endmodule

module Messenger (
  input  Keyboard_IA,
  input  [6:0] Keyboard_Input,
  input  Clock,
  input  [6:0] Key,
  input  Enable,
  input  Output_Clock,
  input  Incoming_Message,
  output Incoming_Monitor_Clock,
  output [6:0] Incoming_Monitor,
  output Display_CLock,
  output [6:0] Outgoing_Monitor,
  output Outgoing_message,
  output Output_command,
  output [6:0] Encrypted_Text
);

  wire Encoder_clock_output;
  wire [6:0] Encrypter_encrypted_message;

  Decrypter Decrypter (.Input_Encrypted_Message(Encrypted_Text), .Private_Key(Key), .Outuput(Incoming_Monitor));
  assign Display_CLock = Keyboard_IA ? Encoder_clock_output : 1'bz;  // Controlled_Buffer controlled_buffer_1
  Encrypter Encrypter (
    .Input_7bit_Ascii(Keyboard_Input), .Private_Key_Input(Key),
    .Encrypted_Message(Encrypter_encrypted_message));
  Encoder Encoder (
    .Clock(Clock), .Enable(Enable), .Output(Outgoing_message), .Input_Available(Keyboard_IA),
    .Clock_Output(Encoder_clock_output), .op_when(Output_command), .ASCII_Data(Encrypter_encrypted_message));
  Decoder Decoder (
    .CLOCK(Clock), .SerialIn(Incoming_Message), .Enable(Enable), .OP_CLOCK(Output_Clock),
    .ASCII(Encrypted_Text), .OP_CLOCK_2(Incoming_Monitor_Clock));

  assign Outgoing_Monitor = Keyboard_Input;
endmodule

module Verfier (
  input  [3:0] _4_Bit_Password,
  input  Switch_Off,
  output Verifier_Output
);

  wire and_1_out, and_2_out, and_3_out, and_4_out, and_5_out, and_6_out, and_7_out, and_8_out, and_9_out,
       nor_1_out, nor_2_out, nor_3_out, nor_4_out, not_1_out, not_2_out, not_3_out, not_4_out, not_5_out,
       not_6_out, not_7_out, not_8_out, not_9_out;

  not not_1 (not_1_out, Switch_Off);
  not not_2 (not_2_out, _4_Bit_Password[3]);
  not not_3 (not_3_out, 1'b0);
  not not_4 (not_4_out, _4_Bit_Password[2]);
  not not_5 (not_5_out, 1'b1);
  not not_6 (not_6_out, _4_Bit_Password[1]);
  not not_7 (not_7_out, 1'b0);
  not not_8 (not_8_out, _4_Bit_Password[0]);
  not not_9 (not_9_out, 1'b1);
  and and_1 (and_1_out, not_2_out, 1'b0);
  and and_2 (and_2_out, _4_Bit_Password[3], not_3_out);
  and and_3 (and_3_out, not_4_out, 1'b1);
  and and_4 (and_4_out, _4_Bit_Password[2], not_5_out);
  and and_5 (and_5_out, not_6_out, 1'b0);
  and and_6 (and_6_out, _4_Bit_Password[1], not_7_out);
  and and_7 (and_7_out, not_8_out, 1'b1);
  and and_8 (and_8_out, _4_Bit_Password[0], not_9_out);
  nor nor_1 (nor_1_out, and_1_out, and_2_out);
  nor nor_2 (nor_2_out, and_3_out, and_4_out);
  nor nor_3 (nor_3_out, and_5_out, and_6_out);
  nor nor_4 (nor_4_out, and_7_out, and_8_out);
  and and_9 (and_9_out, nor_1_out, nor_2_out, nor_3_out, nor_4_out);
  and and_10 (Verifier_Output, and_9_out, not_1_out);

  // Notes on the sheet:
  //   A3
  //   B3
  //   A2
  //   B2
  //   A1
  //   B1
  //   A0
  //   B0
  //   A=B
endmodule

module DeMux (
  input  Switch_Off,
  input  Clock,
  input  Input_Button_Trigger,
  input  S1,
  input  S0,
  output Op_0,
  output Op_1,
  output Op_2,
  output Op_3
);

  wire and_1_out, and_2_out, and_3_out, and_4_out, and_5_out, and_6_out, and_7_out, and_8_out, not_1_out,
       not_2_out;

  not not_1 (not_1_out, S1);
  not not_2 (not_2_out, S0);
  and and_1 (and_1_out, Input_Button_Trigger, not_1_out, not_2_out);
  and and_2 (and_2_out, Input_Button_Trigger, not_1_out, S0);
  and and_3 (and_3_out, Input_Button_Trigger, S1, not_2_out);
  and and_4 (and_4_out, Input_Button_Trigger, S1, S0);
  and and_5 (and_5_out, not_1_out, not_2_out);
  and and_6 (and_6_out, not_1_out, S0);
  and and_7 (and_7_out, not_2_out, not_2_out);
  and and_8 (and_8_out, S0, S0);
  D_Flip_Flop d_ff_1 (.clk(Clock), .D(and_1_out), .Q(Op_0), .en(and_5_out), .reset(Switch_Off));  // open: Qn, preset
  D_Flip_Flop d_ff_2 (.clk(Clock), .D(and_2_out), .Q(Op_1), .en(and_6_out), .reset(Switch_Off));  // open: Qn, preset
  D_Flip_Flop d_ff_3 (.clk(Clock), .D(and_3_out), .Q(Op_2), .en(and_7_out), .reset(Switch_Off));  // open: Qn, preset
  D_Flip_Flop d_ff_4 (.clk(Clock), .D(and_4_out), .Q(Op_3), .en(and_8_out), .reset(Switch_Off));  // open: Qn, preset
endmodule

module _3_Bit_Counter (
  input  Clock,
  input  Switch_Off,
  output Bit___1,
  output Bit___2
);

  J_K_Flip_Flop #(.trigger("falling")) j_k_ff_1 (
    .J(1'b1), .clk(Clock), .K(1'b1), .Q(Bit___1), .reset(Switch_Off));  // open: Qn, preset, en
  J_K_Flip_Flop #(.trigger("falling")) j_k_ff_2 (
    .J(Bit___1), .clk(Clock), .K(Bit___1), .Q(Bit___2), .reset(Switch_Off));  // open: Qn, preset, en
endmodule

module Password_Checker (
  input  Switch_Off,
  input  Clock,
  input  _0_Button,
  input  _1_Button,
  output Verified_Output
);

  wire _3_Bit_Counter_bit___1, _3_Bit_Counter_bit___2, and_1_out, not_1_out, or_1_out;
  wire [3:0] De_Mux_p9;

  and and_1 (and_1_out, not_1_out, _1_Button);
  not not_1 (not_1_out, _0_Button);
  or or_1 (or_1_out, _1_Button, _0_Button);
  _3_Bit_Counter _3_Bit_Counter (
    .Clock(or_1_out), .Switch_Off(Switch_Off), .Bit___1(_3_Bit_Counter_bit___1),
    .Bit___2(_3_Bit_Counter_bit___2));
  // DeMux De_Mux: pin names not known; wires that end beside it: Switch_Off, Clock, and_1_out, _3_Bit_Counter_bit___2, _3_Bit_Counter_bit___1, De_Mux_p9[1], De_Mux_p9[2], De_Mux_p9[3], De_Mux_p9[0]
  Verfier Verifier (._4_Bit_Password(De_Mux_p9), .Switch_Off(Switch_Off), .Verifier_Output(Verified_Output));
endmodule
