// Logisim project Encryption.circ as structural Verilog: 3 circuits, main circuit main
module main (
  input  [6:0] Input,
  input  [6:0] Key,
  output [6:0] out_3
);

  Encrypter encrypter_1 (.Input_7bit_Ascii(Input), .Private_Key_Input(Key), .Encrypted_Message(out_3));
endmodule

module Logical_Left_Bit_shifter (
  input  [2:0] in_1,
  output [2:0] out_2
);


  assign out_2 = {in_1[0], in_1[2:1]};
endmodule

module Encrypter (
  input  [6:0] Input_7bit_Ascii,
  input  [6:0] Private_Key_Input,
  output [6:0] Encrypted_Message
);

  wire [2:0] logical_left_bit_shifter_1_out_2;
  wire [6:0] not_1_out;

  not not_1 (not_1_out[0], Input_7bit_Ascii[0]);
  not not_2 (not_1_out[2], Input_7bit_Ascii[2]);
  not not_3 (not_1_out[4], Input_7bit_Ascii[4]);
  not not_4 (not_1_out[6], Input_7bit_Ascii[6]);
  assign Encrypted_Message = Private_Key_Input ^ {not_1_out[6], logical_left_bit_shifter_1_out_2[2], not_1_out[4], logical_left_bit_shifter_1_out_2[1], not_1_out[2], logical_left_bit_shifter_1_out_2[0], not_1_out[0]};  // XOR_Gate xor_1, 7 bits wide
  Logical_Left_Bit_shifter logical_left_bit_shifter_1 (
    .in_1({Input_7bit_Ascii[5], Input_7bit_Ascii[3], Input_7bit_Ascii[1]}),
    .out_2(logical_left_bit_shifter_1_out_2));

  // Notes on the sheet:
  //   COMMENTS
  //   BIT SHIFTER
  //   Working: 1) Even bits are inverted    2)Odd bits are combined and shifted left     3) The intermediate message is the XORed with private key
  //   <-
  //   |
  //   INTERMEDIATE ENCRYTED MESSAGE
endmodule
