// Logisim project InputOutput.circ as structural Verilog: 2 circuits, main circuit main
module main (
);

  wire clock_1_out, clock_2_out, controlled_buffer_1_out, controlled_buffer_2_out, keyboard_1_avail,
       keyboard_2_avail;
  wire [6:0] Delivery_System_output_a, Delivery_System_output_b, keyboard_1_data, keyboard_2_data;

  TTY tty_1 (.data(keyboard_1_data), .clk(clock_1_out));  // open: we, clr
  assign controlled_buffer_1_out = keyboard_1_avail ? clock_1_out : 1'bz;  // Controlled_Buffer controlled_buffer_1
  Keyboard keyboard_1 (
    .clk(controlled_buffer_1_out), .avail(keyboard_1_avail), .data(keyboard_1_data));  // open: re, clr
  Clock clock_1 (.out(clock_1_out));
  TTY tty_2 (.data(Delivery_System_output_a), .clk(clock_1_out));  // open: we, clr
  Delivery_System Delivery_System (
    .Input_A(keyboard_1_data), .Output_A(Delivery_System_output_a), .Output_B(Delivery_System_output_b),
    .Input_B(keyboard_2_data));
  TTY tty_3 (.data(keyboard_2_data), .clk(clock_2_out));  // open: we, clr
  assign controlled_buffer_2_out = keyboard_2_avail ? clock_2_out : 1'bz;  // Controlled_Buffer controlled_buffer_2
  Keyboard keyboard_2 (
    .clk(controlled_buffer_2_out), .avail(keyboard_2_avail), .data(keyboard_2_data));  // open: re, clr
  Clock clock_2 (.out(clock_2_out));
  TTY tty_4 (.data(Delivery_System_output_b), .clk(clock_2_out));  // open: we, clr

  // Notes on the sheet:
  //   OUTGOING MESSAGE MONITOR A
  //   KEYBOARD A
  //   INCOMING MESSAGE MONITOR A
  //   OUTGOING MESSAGE MONITOR B
  //   KEYBOARD B
  //   INCOMING MESSAGE MONITOR B
endmodule

module Delivery_System (
  input  [6:0] Input_A,
  input  [6:0] Input_B,
  output [6:0] Output_B,
  output [6:0] Output_A
);


  assign Output_A = Input_B;
  assign Output_B = Input_A;
endmodule
