// Logisim project PISO.circ as structural Verilog: 3 circuits, main circuit main
module main (
);

  PISO piso_1 ();  // open: SerialIN, Clock, Shift_Load, D6, D5, D4, D3, D2, D1, D0, Enable, Clear, SerialOut
endmodule

module PISO (
  input  D6,
  input  D5,
  input  D4,
  input  D3,
  input  D2,
  input  D1,
  input  D0,
  input  SerialIN,
  input  Clock,
  input  Shift_Load,
  input  Enable,
  input  Clear,
  output SerialOut
);

  wire n1_bit_register_1_q, n1_bit_register_2_q, n1_bit_register_3_q, n1_bit_register_4_q,
       n1_bit_register_5_q, n1_bit_register_6_q;

  _1_bit_Register u_1_bit_register_1 (
    .CLock(Clock), .SerialIn(SerialIN), .SHIFT_LOAD(Shift_Load), .Din(D6), .Enable(Enable), .Clear(Clear),
    .Q(n1_bit_register_1_q));
  _1_bit_Register u_1_bit_register_2 (
    .CLock(Clock), .SerialIn(n1_bit_register_1_q), .SHIFT_LOAD(Shift_Load), .Din(D5), .Enable(Enable),
    .Clear(Clear), .Q(n1_bit_register_2_q));
  _1_bit_Register u_1_bit_register_3 (
    .CLock(Clock), .SerialIn(n1_bit_register_2_q), .SHIFT_LOAD(Shift_Load), .Din(D4), .Enable(Enable),
    .Clear(Clear), .Q(n1_bit_register_3_q));
  _1_bit_Register u_1_bit_register_4 (
    .CLock(Clock), .SerialIn(n1_bit_register_3_q), .SHIFT_LOAD(Shift_Load), .Din(D3), .Enable(Enable),
    .Clear(Clear), .Q(n1_bit_register_4_q));
  _1_bit_Register u_1_bit_register_5 (
    .CLock(Clock), .SerialIn(n1_bit_register_4_q), .SHIFT_LOAD(Shift_Load), .Din(D2), .Enable(Enable),
    .Clear(Clear), .Q(n1_bit_register_5_q));
  _1_bit_Register u_1_bit_register_6 (
    .CLock(Clock), .SerialIn(n1_bit_register_5_q), .SHIFT_LOAD(Shift_Load), .Din(D1), .Enable(Enable),
    .Clear(Clear), .Q(n1_bit_register_6_q));
  _1_bit_Register u_1_bit_register_7 (
    .CLock(Clock), .SerialIn(n1_bit_register_6_q), .SHIFT_LOAD(Shift_Load), .Din(D0), .Enable(Enable),
    .Clear(Clear), .Q(SerialOut));
endmodule

module _1_bit_Register (
  input  Din,
  input  CLock,
  input  SerialIn,
  input  SHIFT_LOAD,
  input  Enable,
  input  Clear,
  output Q
);

  wire and_1_out, and_2_out, not_1_out, or_1_out;

  not not_1 (not_1_out, SHIFT_LOAD);
  and and_1 (and_1_out, Din, not_1_out);
  and and_2 (and_2_out, SHIFT_LOAD, SerialIn);
  D_Flip_Flop d_ff_1 (.clk(CLock), .D(or_1_out), .Q(Q), .en(Enable), .reset(Clear));  // open: Qn, preset
  or or_1 (or_1_out, and_1_out, and_2_out);
endmodule
